// Logisim project [016][M2].circ as structural Verilog: 3 circuits, main circuit ALU
module ALU (
  input  [15:0] AC,
  input  [15:0] DR,
  input  [3:0] Sel,
  input  [7:0] INPR,
  output [15:0] Output,
  output E
);

  wire adder_1_cout, subtractor_1_bout;
  wire [15:0] adder_1_out, and_1_out, bit_extender_1_out, not_1_out, or_1_out, shifter_1_out, shifter_2_out,
       subtractor_1_out, xor_1_out;

  assign and_1_out = AC & DR;  // AND_Gate and_1, 16 bits wide
  assign bit_extender_1_out = {{8{1'b0}}, INPR};  // Bit_Extender bit_extender_1
  assign or_1_out = AC | DR;  // OR_Gate or_1, 16 bits wide
  Adder #(.width(16)) adder_1 (.a(AC), .b(DR), .out(adder_1_out), .cin(1'b0), .cout(adder_1_cout));
  Subtractor #(.width(16)) subtractor_1 (.a(AC), .b(DR), .out(subtractor_1_out), .bin(1'b0), .bout(subtractor_1_bout));
  assign not_1_out = ~AC;  // NOT_Gate not_1, 16 bits wide
  assign xor_1_out = DR ^ AC;  // XOR_Gate xor_1, 16 bits wide
  Shifter #(.width(16)) shifter_1 (.in(AC), .\dist (4'b0001), .out(shifter_1_out));
  Shifter #(.width(16), .shift("lr")) shifter_2 (.in(AC), .\dist (4'b0001), .out(shifter_2_out));
  Multiplexer #(.select(4), .width(16)) multiplexer_1 (
    .in0(and_1_out), .in1(or_1_out), .in2(adder_1_out), .in3(subtractor_1_out), .in4(DR), .in5(not_1_out),
    .in6(xor_1_out), .in7(shifter_1_out), .in8(shifter_2_out), .in9(bit_extender_1_out), .out(Output),
    .sel(Sel), .en(1'b1));  // open: in10, in11, in12, in13, in14, in15
  Multiplexer multiplexer_2 (.in0(adder_1_cout), .in1(subtractor_1_bout), .out(E), .sel(Sel[0]), .en(1'b1));
endmodule

module Bus_System (
  output E
);

  wire AC, AR, button_1_out, CIL, CIR, CLAC, CLAR, CLE, clock, CLPC, CLSC, d_ff_6_q, d_ff_7_q, E_prime, EAL,
       FGI, INAC, INAR, INDR, INPC, lcu_1_s, LDAC, LDAR, LDDR, LDE, LDIR, LDOUTR, LDPC, LDTR,
       multiplexer_1_out, multiplexer_2_out, or_1_out, or_2_out, p, PC, R, READ, SC, SIN, WRITE;
  wire [2:0] BUSSEL;
  wire [3:0] ALUSEL, SCOUT;
  wire [6:0] keyboard_1_data;
  wire [7:0] bit_extender_1_out, INPR_q, Keyboard, O;
  wire [11:0] AR_q, bit_extender_2_out, bit_extender_3_out, PC_q;
  wire [15:0] ACIN, ACOUT, ALUAC, bit_extender_4_out, bit_extender_5_out, DROUT, IROUT, multiplexer_3_out,
       multiplexer_5_out, ram_1_data, TR_q;

  Counter INPR (.load(FGI), .D(Keyboard), .count(1'b0), .Q(INPR_q), .clk(clock), .clr(1'b0));  // open: carry
  Bit_Extender #(.in_width(16), .out_width(8)) bit_extender_1 (.in(multiplexer_5_out), .out(bit_extender_1_out));
  Multiplexer #(.enable("false")) multiplexer_1 (.in0(ACOUT[0]), .in1(ACOUT[15]), .out(multiplexer_1_out), .sel(CIL));
  Bit_Extender #(.in_width(16), .out_width(12)) bit_extender_2 (.in(multiplexer_5_out), .out(bit_extender_2_out));
  Bit_Extender #(.in_width(16), .out_width(12)) bit_extender_3 (.in(multiplexer_5_out), .out(bit_extender_3_out));
  ALU ALU (.AC(ACOUT), .DR(DROUT), .INPR(INPR_q), .Sel(ALUSEL), .Output(ALUAC), .E(EAL));
  Counter OUTR (.load(LDOUTR), .D(bit_extender_1_out), .count(1'b0), .Q(O), .clk(clock), .clr(1'b0));  // open: carry
  Multiplexer #(.enable("false")) multiplexer_2 (
    .in0(EAL), .in1(multiplexer_1_out), .out(multiplexer_2_out), .sel(or_1_out));
  or or_1 (or_1_out, CIL, CIR);
  D_Flip_Flop d_ff_1 (.clk(clock), .D(multiplexer_2_out), .Q(E), .Qn(E_prime), .en(LDE), .reset(CLE));  // open: preset
  Counter #(.width(12), .max('hfff)) u_AR (
    .load(LDAR), .D(bit_extender_2_out), .count(INAR), .Q(AR_q), .clk(clock), .clr(AR));  // open: carry
  Counter #(.width(12), .max('hfff)) u_PC (
    .load(LDPC), .D(bit_extender_3_out), .count(INPC), .Q(PC_q), .clk(clock), .clr(PC));  // open: carry
  Counter #(.width(16), .max('hffff)) DR (
    .load(LDDR), .D(multiplexer_5_out), .count(INDR), .Q(DROUT), .clk(clock), .clr(1'b0));  // open: carry
  Counter #(.width(16), .max('hffff)) u_AC (
    .load(LDAC), .D(ACIN), .count(INAC), .Q(ACOUT), .clk(clock), .clr(AC));  // open: carry
  Counter #(.width(16), .max('hffff)) IR (
    .load(LDIR), .D(multiplexer_5_out), .count(1'b0), .Q(IROUT), .clk(clock), .clr(1'b0));  // open: carry
  Counter #(.width(16), .max('hffff)) TR (
    .load(LDTR), .D(multiplexer_5_out), .count(1'b0), .Q(TR_q), .clk(clock), .clr(1'b0));  // open: carry
  RAM #(.addrWidth(12), .dataWidth(16), .bus("separate")) ram_1 (
    .addr(AR_q), .din(multiplexer_5_out), .data(ram_1_data), .str(WRITE), .clk(clock), .ld(READ));  // open: sel, clr
  assign bit_extender_4_out = {{4{1'b0}}, AR_q};  // Bit_Extender bit_extender_4
  assign bit_extender_5_out = {{4{1'b0}}, PC_q};  // Bit_Extender bit_extender_5
  Multiplexer #(.width(16), .enable("false")) multiplexer_3 (
    .in0({E, ALUAC[14:0]}), .in1({ALUAC[15:1], E}), .out(multiplexer_3_out), .sel(CIL));
  Multiplexer #(.width(16), .enable("false")) multiplexer_4 (
    .in0(ALUAC), .in1(multiplexer_3_out), .out(ACIN), .sel(or_2_out));
  or or_2 (or_2_out, CIL, CIR);
  Clock clock_1 (.out(clock));
  Multiplexer #(.select(3), .width(16)) multiplexer_5 (
    .in1(bit_extender_4_out), .in2(bit_extender_5_out), .in3(DROUT), .in4(ACOUT), .in5(IROUT), .in6(TR_q),
    .in7(ram_1_data), .out(multiplexer_5_out), .sel(BUSSEL), .en(1'b1));  // open: in0
  Button button_1 (.out(button_1_out));
  D_Flip_Flop d_ff_2 (.clk(clock), .D(CLAR), .Q(AR));  // open: Qn, preset, en, reset
  D_Flip_Flop d_ff_3 (.clk(clock), .D(CLPC), .Q(PC));  // open: Qn, preset, en, reset
  D_Flip_Flop d_ff_4 (.clk(clock), .D(CLAC), .Q(AC));  // open: Qn, preset, en, reset
  D_Flip_Flop d_ff_5 (.clk(clock), .D(CLSC), .Q(SC));  // open: Qn, preset, en, reset
  D_Flip_Flop S (.clk(clock), .Q(SIN), .preset(button_1_out), .reset(d_ff_6_q));  // open: D, Qn, en
  D_Flip_Flop d_ff_6 (.clk(clock), .Q(d_ff_6_q), .preset(lcu_1_s), .en(1'b1), .reset(1'b0));  // open: D, Qn
  Counter #(.width(4), .max('hf)) u_SC (.count(SIN), .Q(SCOUT), .clk(clock), .clr(SC));  // open: load, D, carry
  Keyboard #(.buflen(1)) keyboard_1 (.clk(clock), .re(p), .avail(FGI), .data(keyboard_1_data));  // open: clr
  TTY #(.rows(15), .cols(50)) tty_1 (.data(O[6:0]), .clk(clock), .we(d_ff_7_q));  // open: clr
  D_Flip_Flop d_ff_7 (.clk(clock), .D(LDOUTR), .Q(d_ff_7_q));  // open: Qn, preset, en, reset
  LCU lcu_1 (
    .LDDR(LDDR), .INDR(INDR), .LDIR(LDIR), .INAR(INAR), .LDAR(LDAR), .CLAR(CLAR), .CLPC(CLPC), .LDPC(LDPC),
    .LDAC(LDAC), .CLCK(clock), .CLAC(CLAC), .INAC(INAC), .READ(READ), .WRITE(WRITE), .IROUT(IROUT),
    .SC(SCOUT), .INPC(INPC), .DROUT(DROUT), .ACOUT(ACOUT), .E_prime(E_prime), .LDTR(LDTR), .LDOUTR(LDOUTR),
    .CLSC(CLSC), .CLE(CLE), .LDE(LDE), .S(lcu_1_s), .CIR(CIR), .CIL(CIL), .FGI(FGI), .FGO(1'b1), .R(R),
    .SIN(SIN), .ALUSEL(ALUSEL), .BUSSEL(BUSSEL), .p(p));
  assign Keyboard = {{1{1'b0}}, keyboard_1_data};  // Bit_Extender bit_extender_6

  // Other names for the same wires on the sheet: EOUT = E

  // Notes on the sheet:
  //   To start
  //   Mohamed Sabry 37-18341 T-32
  //   Abdelrahman Gharib El Hamahmi 37-15881 T-11
  //   Team 16 :
  //   Nesrin Abdulaziz Attia 37-16218  T-13
  //   Olfat Mostafa Abdelaziz 37-19029 T-17
endmodule

module LCU (
  input  [15:0] ACOUT,
  input  SIN,
  input  [15:0] IROUT,
  input  [15:0] DROUT,
  input  [3:0] SC,
  input  E_prime,
  input  CLCK,
  input  FGO,
  input  FGI,
  output INDR,
  output p,
  output CLE,
  output LDDR,
  output [2:0] BUSSEL,
  output INAC,
  output LDOUTR,
  output LDE,
  output WRITE,
  output CLAC,
  output LDTR,
  output LDIR,
  output LDAC,
  output [3:0] ALUSEL,
  output S,
  output CLPC,
  output INPC,
  output READ,
  output CLAR,
  output CIR,
  output CIL,
  output CLSC,
  output R,
  output INAR,
  output LDAR,
  output LDPC
);

  wire ACOR, and_2_out, and_3_out, and_4_out, and_5_out, and_9_out, and_10_out, and_11_out, and_12_out,
       and_13_out, and_14_out, and_15_out, and_16_out, and_18_out, and_19_out, and_24_out, and_25_out,
       and_26_out, and_27_out, and_28_out, and_29_out, and_30_out, and_31_out, and_33_out, and_36_out,
       and_37_out, and_38_out, and_39_out, and_40_out, and_41_out, and_44_out, and_45_out, and_46_out,
       and_47_out, and_48_out, and_50_out, and_51_out, and_54_out, and_55_out, and_56_out, and_57_out,
       and_58_out, and_59_out, and_60_out, and_61_out, and_62_out, and_63_out, and_64_out, and_65_out,
       and_66_out, and_67_out, and_68_out, and_69_out, and_70_out, and_71_out, D0, D1, D2, D3, D4, D5, D6,
       D7, decoder_1_out0, DROR, FGI_t, FGO_t, I, I_prime, IEN, or_1_out, or_2_out, or_5_out, or_10_out,
       or_12_out, or_14_out, or_15_out, or_16_out, or_18_out, or_20_out, r_t, T0, T1, T2, T3, T4, T5, T6, T7;

  and and_1 (r_t, D7, I_prime, T3);
  Decoder #(.select(4), .enable("false")) decoder_1 (
    .out0(decoder_1_out0), .out1(T1), .out2(T2), .out3(T3), .out4(T4), .out5(T5), .out6(T6), .out7(T7),
    .sel(SC));  // open: out8, out9, out10, out11, out12, out13, out14, out15
  and and_2 (and_2_out, p, IROUT[7]);
  and and_3 (and_3_out, p, IROUT[6]);
  and and_4 (and_4_out, R, T2);
  D_Flip_Flop u_FGO (.clk(CLCK), .Q(FGO_t), .preset(FGO), .reset(and_5_out));  // open: D, Qn, en
  and and_5 (and_5_out, p, IROUT[10]);
  and and_6 (p, D7, I, T3);
  and and_7 (T0, SIN, decoder_1_out0);
  and and_8 (S, r_t, IROUT[0]);
  J_K_Flip_Flop u_IEN (.J(and_2_out), .clk(CLCK), .K(or_1_out), .Q(IEN), .en(1'b1), .reset(1'b0));  // open: Qn, preset
  or or_1 (or_1_out, and_3_out, and_4_out);
  and and_9 (and_9_out, D3, T4);
  and and_10 (and_10_out, D5, T4);
  and and_11 (and_11_out, T6, D6);
  or or_2 (or_2_out, D0, D1, D2, D6);
  and and_12 (and_12_out, ~R, T1);  // AND_Gate
  and and_13 (and_13_out, T3, ~D7, I);  // AND_Gate
  D_Flip_Flop u_FGI (.clk(CLCK), .Q(FGI_t), .preset(FGI), .reset(and_14_out));  // open: D, Qn, en
  and and_14 (and_14_out, p, IROUT[11]);
  and and_15 (and_15_out, T1, R);
  or or_3 (WRITE, and_15_out, and_9_out, and_10_out, and_11_out);
  and and_16 (and_16_out, or_2_out, T4);
  or or_4 (READ, and_16_out, and_12_out, and_13_out);
  and and_17 (CLAR, T0, R);
  and and_18 (and_18_out, ~R, or_5_out);  // AND_Gate
  or or_5 (or_5_out, T0, T2);
  and and_19 (and_19_out, T3, ~D7, I);  // AND_Gate
  and and_20 (INAR, D5, T4);
  or or_6 (LDAR, and_18_out, and_19_out);
  or or_7 (ACOR, ACOUT[0], ACOUT[1], ACOUT[2], ACOUT[3], ACOUT[4], ACOUT[5], ACOUT[6], ACOUT[7], ACOUT[9], ACOUT[10], ACOUT[11], ACOUT[12], ACOUT[13], ACOUT[14], ACOUT[15], ACOUT[8]);
  or or_8 (DROR, DROUT[0], DROUT[1], DROUT[2], DROUT[3], DROUT[4], DROUT[5], DROUT[6], DROUT[7], DROUT[9], DROUT[10], DROUT[11], DROUT[12], DROUT[13], DROUT[14], DROUT[15], DROUT[8]);
  and and_21 (LDOUTR, IROUT[10], p);
  and and_22 (LDTR, T0, R);
  and and_23 (LDIR, T1, ~R);  // AND_Gate
  and and_24 (and_24_out, R, T2);
  and and_25 (and_25_out, D6, ~DROR, T6);  // AND_Gate
  and and_26 (and_26_out, r_t, ~ACOUT[15], IROUT[4]);  // AND_Gate
  and and_27 (and_27_out, IROUT[9], p, FGI_t);
  and and_28 (and_28_out, r_t, ACOUT[15], IROUT[3]);
  and and_29 (and_29_out, r_t, E_prime, IROUT[1]);
  and and_30 (and_30_out, D4, T4);
  or or_9 (LDPC, and_30_out, and_31_out);
  and and_31 (and_31_out, D5, T5);
  or or_10 (or_10_out, D0, D1, D2, D6);
  and and_32 (LDDR, or_10_out, T4);
  and and_33 (and_33_out, ~R, T1);  // AND_Gate
  or or_11 (INPC, and_33_out, and_24_out, and_25_out, and_26_out, and_28_out, and_29_out, and_27_out, and_39_out, and_40_out);
  and and_34 (INDR, D6, T5);
  and and_35 (INAC, IROUT[5], r_t);
  or or_12 (or_12_out, D0, D1, D2);
  and and_36 (and_36_out, or_12_out, T5);
  or or_13 (LDAC, and_36_out, and_37_out, and_38_out);
  and and_37 (and_37_out, r_t, or_14_out);
  or or_14 (or_14_out, IROUT[9], IROUT[6], IROUT[7]);
  and and_38 (and_38_out, IROUT[11], p);
  and and_39 (and_39_out, r_t, ~ACOR, IROUT[2]);  // AND_Gate
  and and_40 (and_40_out, IROUT[8], p, FGO_t);
  and and_41 (and_41_out, ~T0, ~T1, ~T2, IEN, or_15_out);  // AND_Gate
  or or_15 (or_15_out, FGI_t, FGO_t);
  and and_42 (CLAC, IROUT[11], r_t);
  and and_43 (CLPC, R, T1);
  D_Flip_Flop u_R (.clk(CLCK), .D(and_41_out), .Q(R), .reset(and_44_out));  // open: Qn, preset, en
  and and_44 (and_44_out, R, T2);
  D_Flip_Flop d_ff_1 (.clk(CLCK), .D(IROUT[15]), .Q(I), .Qn(I_prime));  // open: preset, en, reset
  Decoder #(.select(3), .enable("false")) decoder_2 (
    .out0(D0), .out1(D1), .out2(D2), .out3(D3), .out4(D4), .out5(D5), .out6(D6), .out7(D7), .sel(IROUT[14:12]));
  and and_45 (and_45_out, D6, T6);
  and and_46 (and_46_out, T5, or_16_out);
  or or_16 (or_16_out, D0, D1, D2, D5);
  and and_47 (and_47_out, R, T2);
  or or_17 (CLSC, and_47_out, and_45_out, p, r_t, and_46_out, and_48_out);
  and and_48 (and_48_out, T4, or_18_out);
  or or_18 (or_18_out, D3, D4);
  and and_49 (CLE, r_t, IROUT[10]);
  and and_50 (and_50_out, D1, T5);
  or or_19 (LDE, and_50_out, and_51_out);
  and and_51 (and_51_out, r_t, or_20_out);
  or or_20 (or_20_out, IROUT[6], IROUT[7]);
  and and_52 (CIR, IROUT[7], r_t);
  and and_53 (CIL, IROUT[6], r_t);
  and and_54 (and_54_out, D3, T4);
  and and_55 (and_55_out, p, IROUT[10]);
  or or_21 (BUSSEL[2], and_54_out, and_55_out, and_56_out, and_57_out, READ);
  and and_56 (and_56_out, ~R, T2);  // AND_Gate
  and and_57 (and_57_out, R, T1);
  and and_58 (and_58_out, T1, R);
  or or_22 (BUSSEL[0], READ, and_68_out, and_69_out, and_71_out, and_70_out);
  or or_23 (BUSSEL[1], READ, and_58_out, and_59_out, and_60_out, T0);
  and and_59 (and_59_out, T6, D6);
  and and_60 (and_60_out, D5, T4);
  and and_61 (and_61_out, D0, T5);
  and and_62 (and_62_out, D1, T5);
  and and_63 (and_63_out, D2, T5);
  and and_64 (and_64_out, r_t, IROUT[9]);
  and and_65 (and_65_out, r_t, IROUT[6]);
  and and_66 (and_66_out, IROUT[7], r_t);
  and and_67 (and_67_out, IROUT[11], p);
  and and_68 (and_68_out, D4, T4);
  and and_69 (and_69_out, D5, T5);
  and and_70 (and_70_out, T2, ~R);  // AND_Gate
  and and_71 (and_71_out, D6, T6);
  Priority_Encoder #(.select(4)) priority_encoder_1 (
    .in0(and_61_out), .in1(1'b0), .in2(and_62_out), .in3(1'b0), .in4(and_63_out), .in5(and_64_out),
    .in6(1'b0), .in7(and_65_out), .in8(and_66_out), .in9(and_67_out), .in10(1'b0), .in11(1'b0), .in12(1'b0),
    .in13(1'b0), .in14(1'b0), .in15(1'b0), .out(ALUSEL), .en_in(1'b1));  // open: gs, en_out

  // Other names for the same wires on the sheet: AC_0 = ACOUT[0]; AC_15 = ACOUT[15]; CLK = CLCK; B0 = IROUT[0];
  //   B1 = IROUT[1]; B2 = IROUT[2]; B3 = IROUT[3]; B4 = IROUT[4]; B5 = IROUT[5]; B6 = IROUT[6]; B7 = IROUT[7];
  //   B8 = IROUT[8]; B9 = IROUT[9]; B10 = IROUT[10]; B11 = IROUT[11]; MREAD = READ
endmodule
